# Fritzing sketch Vernier_PhotoGateBuild (saved by Fritzing 0.9.3b)

parts:
  SparkFun_Serial_LCD_Kit1 = Serial LCD Kit [part_number=LCD-10097 package="DIP (Dual Inline) [THT]"]
  Part1 = FTDI Basic Programmer
  PART1 = LED Tactile Button Breakout [part_number=BOB-10467]
  JP1 = Header 1 [package=1x01_offset]
  JP2 = Header 1 [package=1x01_offset]  # not connected
  JP3 = Header 1 [package=1x01_offset]
  JP4 = Header 1 [package=1x01_offset]  # not connected
  JP5 = Header 1 [package=1x01_offset]  # not connected
  JP6 = Header 1 [package=1x01_offset]
  S1 = Momentary Switch [package=ksa_sealed_tac_switch]

nets:
  N1: SparkFun_Serial_LCD_Kit1.5V#3, JP3.1
  N2: SparkFun_Serial_LCD_Kit1.GND#4, PART1.C, PART1.B1, JP6.1, S1.2
  N3: SparkFun_Serial_LCD_Kit1.D10, JP1.1
  N4: SparkFun_Serial_LCD_Kit1.D12, PART1.B2
  N5: SparkFun_Serial_LCD_Kit1.D13, PART1.A
  N6: SparkFun_Serial_LCD_Kit1.RST, S1.4
  N7: SparkFun_Serial_LCD_Kit1.GND#18, Part1.GND
  N8: SparkFun_Serial_LCD_Kit1.GND#19, Part1.CTS
  N9: SparkFun_Serial_LCD_Kit1.5V#20, Part1.POWER
  N10: SparkFun_Serial_LCD_Kit1.RXI, Part1.TXO
  N11: SparkFun_Serial_LCD_Kit1.TXO, Part1.RXI
  N12: SparkFun_Serial_LCD_Kit1.DTR, Part1.DTR

notes:
  Vernier Cable - pin 1 is on top
  RESET
  Connect to barrel jack for connecting to external battery pack.

custom parts:
  Serial LCD Kit: Calling this the "Serial Enabled LCD Kit" doesn't do justice to how cool it actually is. After you've assembled this all-PTH kit, you'll be left with a fully Arduino-compatible development board that just happens to have a white on black 16x2 display built-in. Turns out the ATMega328 is pretty far over-spec for just controlling a parallel LCD so there's a lot of horsepower left over to do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
  LED Tactile Button Breakout: This simple breakout board makes it easy to use our LED tactile switches in a breadboard, or your next project. Please visit sparkfun.com for more information.
